# Fritzing sketch Ethernet_shield_with_Arduino_Mega_and_RFM95 (saved by Fritzing 0.9.3b)

parts:
  Part1 = Adafruit RFM9x LoRa Radio [part_number="Adafruit #3072 and #3073"]
  Part2 = Arduino Mega ADK (Rev3)
  Part3 = Adafruit Feather M0 RFM9x LoRa [part_number="Adafruit #3178 or #3179"]
  R1 = Resistor [tolerance=±5% resistance=220 package="1206 [SMD]"]
  LED1 = smd LED [color="Red (633nm)" package="1206 [SMD]"]
  ANT1 = Antenna
  ANT2 = Antenna
  Part4 = Adafruit Feather M0 RFM9x LoRa [part_number="Adafruit #3178 or #3179"]
  ANT3 = Antenna
  Part6 = MQ-3 breakout
  U1 = BATTERY-2 [package=battery-aaa]
  Part7 = Adafruit SHT31-D Sensirion Temperature/Humidity Sensor [part_number="Adafruit #2857"]
  Part8 = Arduino Ethernet Shield (Rev3)
  Power_plug1 = Power plug

nets:
  N1: Part1.ANTENNA, ANT2.antenna_lead
  N2: Part1.GND, Part1.EN
  N3: Part1.DIO0, Part2.D2_PWM
  N4: Part1.CS, Part2.D4_PWM
  N5: Part1.RST, Part2.D3_PWM
  N6: Part2.GND#283, Part2.GND#307, Part2.GND#308, LED1.cathode, Power_plug1.GND
  N7: Part2.D13_PWM, R1.Pin_1
  VIN: Part2.VIN, Power_plug1.VCC
  N8: Part2.D53/SS, Part8.ETH_CS
  N9: Part2.5V#501, Part8.5V
  N10: Part2.ICSP_SCK, Part8.ICSP_SCK
  N11: Part2.ICSP_MOSI, Part8.ICSP_MOSI
  N12: Part2.RESET3, Part8.ICSP_MISO
  N13: Part2.GND#505, Part8.GND
  N14: Part3.ANT, ANT1.antenna_lead
  N15: Part4.ANT, ANT3.antenna_lead
  GND: Part4.GND, Part7.GND
  +3V3: Part4.+3V3, Part7.VIN
  N16: Part4.SCL, Part7.SCL
  N17: Part4.SDA, Part7.SDA
  N18: Part6.GND, U1.-1

notes:
  Node1
  Node2
  Gataway

custom parts:
  Adafruit RFM9x LoRa Radio: Sending data over long distances is like magic, and now you can be a magician with this range of powerful and easy-to-use radio modules. Sure, sometimes you want to talk to a computer (a good time to use WiFi) or perhaps communicate with a Phone (choose Bluetooth Low Energy!) but what if you want to send data very far? Most WiFi, Bluetooth, Zigbee and other wireless chipsets use 2.4GHz, which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
  Adafruit Feather M0 RFM9x LoRa: This is the Adafruit Feather M0 RFM95 LoRa Radio - our take on an microcontroller with a "Long Range (LoRa)" packet radio transceiver with built in USB and battery charging. Its an Adafruit Feather M0 with a 433Mhz or 900MHz radio module cooked in! Great for making wireless networks that are more flexible than Bluetooth LE and without the high power requirements of WiFi. We have other boards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
  MQ-3 breakout: Alcohol sensor is capable of detecting alcohol (ethanol) particles on itself and gives the information in digital form back to us to manipulate with it. SKU:101251 • Voltage: 5V DC • Power: max 750mW • Measurement range: 0.04-4mg/L
  Adafruit SHT31-D Sensirion Temperature/Humidity Sensor: Sensirion Temperature/Humidity sensors are some of the finest & highest-accuracy devices you can get. And, finally we have some that have a true I2C interface for easy reading. The SHT31-D sensor has an excellent ±2% relative humidity and ±0.3°C accuracy for most uses. Unlike earlier SHT sensors, this sensor has a true I2C interface, and (bonus!) even with two address options. It also is 3V or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
