# Fritzing sketch Arduino_Mega_With_ADAFRUIT_RFM95W_LORA_AND_Feather_Module (saved by Fritzing 0.9.3b)

parts:
  Part1 = Adafruit RFM9x LoRa Radio [part_number="Adafruit #3072 and #3073"]
  Part2 = Arduino Mega ADK (Rev3)
  Part3 = Adafruit Feather M0 RFM9x LoRa [part_number="Adafruit #3178 or #3179"]
  R1 = Resistor [tolerance=±5% resistance=220 package="1206 [SMD]"]
  LED1 = smd LED [color="Red (633nm)" package="1206 [SMD]"]
  ANT1 = Antenna
  ANT2 = Antenna
  U1 = LIPO-1000mAh [package=lipo-1000]  # not connected

nets:
  N1: Part1.ANTENNA, ANT2.antenna_lead
  N2: Part1.DIO0, Part2.D2_PWM
  N3: Part1.CS, Part2.D4_PWM
  N4: Part1.RST, Part2.D3_PWM
  N5: Part2.GND, LED1.cathode
  N6: Part2.D13_PWM, R1.Pin_1
  N7: Part3.ANT, ANT1.antenna_lead

custom parts:
  Adafruit RFM9x LoRa Radio: Sending data over long distances is like magic, and now you can be a magician with this range of powerful and easy-to-use radio modules. Sure, sometimes you want to talk to a computer (a good time to use WiFi) or perhaps communicate with a Phone (choose Bluetooth Low Energy!) but what if you want to send data very far? Most WiFi, Bluetooth, Zigbee and other wireless chipsets use 2.4GHz, which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
  Adafruit Feather M0 RFM9x LoRa: This is the Adafruit Feather M0 RFM95 LoRa Radio - our take on an microcontroller with a "Long Range (LoRa)" packet radio transceiver with built in USB and battery charging. Its an Adafruit Feather M0 with a 433Mhz or 900MHz radio module cooked in! Great for making wireless networks that are more flexible than Bluetooth LE and without the high power requirements of WiFi. We have other boards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
